# Fritzing sketch 2.1. Upravljacki dio sustava s mikrokontrolerom (saved by Fritzing 0.9.3b)

parts:
  M1 = ESP32-C3-DevKitM-1 [part_number=ESP32-C3-DevKitM-1]
  M2 = ESP-Prog [package=THT]

nets:
  N1: M1.GND-1, M1.GND-12, M2.JTAG-GND-9-.1, M2.JTAG-GND-7-1.27
  N2: M1.4, M2.JTAG-ESP_TMS-.1
  N3: M1.5, M2.JTAG-ESP_TDI-.1
  N4: M1.6, M2.JTAG-ESP-TCK-.1
  N5: M1.7, M2.JAG-ESP-TDO-.1

custom parts:
  ESP32-C3-DevKitM-1: The DOIT Esp32 DevKit v1 is one of the development board created by DOIT to evaluate the ESP-WROOM-32 module. It is based on the ESP32 microcontroller that boasts Wifi, Bluetooth, Ethernet and Low Power support all in a single chip. (vanepp) Feb 2021: converted to ESP32-C3-DevKitM-1. This chip is 30pins long (2 x15) and 11 pins width.
  ESP-Prog: Espressif ESP-Prog board. ESP-Prog is one of Espressif’s development and debugging tools, with functions including automatic firmware downloading, serial communication, and JTAG online debugging. ESP-Prog's automatic firmware downloading and serial communication functions are supported on both the ESP8266 and ESP32 platforms, while the JTAG online debugging is supported only on the ESP32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
