# Fritzing sketch 2.1.1. Ultrazvucni senzor udaljenosti (saved by Fritzing 0.9.3b)

parts:
  M1 = ESP32-C3-DevKitM-1 [part_number=ESP32-C3-DevKitM-1]
  hc-sr1 = hc-sr04

nets:
  N1: M1.GND-12, M1.GND-23, hc-sr1.GND
  N2: M1.0, hc-sr1.Echo
  N3: M1.1, hc-sr1.Trig
  N4: M1.10, hc-sr1.VCC

custom parts:
  ESP32-C3-DevKitM-1: The DOIT Esp32 DevKit v1 is one of the development board created by DOIT to evaluate the ESP-WROOM-32 module. It is based on the ESP32 microcontroller that boasts Wifi, Bluetooth, Ethernet and Low Power support all in a single chip. (vanepp) Feb 2021: converted to ESP32-C3-DevKitM-1. This chip is 30pins long (2 x15) and 11 pins width.
