# Fritzing sketch 2.1.2. Senzor infracrvene svjetlosti (saved by Fritzing 0.9.3b)

parts:
  M1 = ESP32-C3-DevKitM-1 [part_number=ESP32-C3-DevKitM-1]
  LED1 = LED - 5mm [color="Infrared (940nm)" package="5 mm [THT]"]
  R1 = Resistor [tolerance=±5% resistance=100 package="0805 [SMD]"]
  LED2 = Photodiode 5mm Black [package="5 mm [THT]"]
  R2 = Resistor [tolerance=±2% resistance=10k package=THT]

nets:
  N1: M1.GND-15, M1.GND-23, LED1.cathode, R2.Pin_0
  N2: M1.0, LED2.anode, R2.Pin_1
  N3: M1.1, LED2.cathode
  N4: M1.10, R1.Pin_1
  N5: LED1.anode, R1.Pin_0

custom parts:
  ESP32-C3-DevKitM-1: The DOIT Esp32 DevKit v1 is one of the development board created by DOIT to evaluate the ESP-WROOM-32 module. It is based on the ESP32 microcontroller that boasts Wifi, Bluetooth, Ethernet and Low Power support all in a single chip. (vanepp) Feb 2021: converted to ESP32-C3-DevKitM-1. This chip is 30pins long (2 x15) and 11 pins width.
  Photodiode 5mm Black: Photodiode 5mm Black/ Transparent
