# Fritzing sketch 2.3. Pracenje stanja baterije (saved by Fritzing 0.9.3b)

parts:
  M1 = ESP32-C3-DevKitM-1 [part_number=ESP32-C3-DevKitM-1]
  hc-sr1 = hc-sr04
  YwRobot_Power_Supply1 = YwRobot Breadboard Power Supply [part_number=545043]
  VCC1 = Battery block 9V
  R1 = Resistor [tolerance=±2% resistance=10k package=THT]
  R2 = Resistor [tolerance=±2% resistance=1k package=THT]

nets:
  GND: M1.GND-12, M1.GND-16, M1.GND-23, hc-sr1.GND, YwRobot_Power_Supply1.GND
  N1: M1.3V3-17, YwRobot_Power_Supply1.VCC
  N2: M1.2, R1.Pin_1, R2.Pin_1
  N3: M1.0, hc-sr1.Echo
  N4: M1.1, hc-sr1.Trig
  N5: M1.10, hc-sr1.VCC
  N6: VCC1.-, R1.Pin_0
  N7: VCC1.+, R2.Pin_0

custom parts:
  ESP32-C3-DevKitM-1: The DOIT Esp32 DevKit v1 is one of the development board created by DOIT to evaluate the ESP-WROOM-32 module. It is based on the ESP32 microcontroller that boasts Wifi, Bluetooth, Ethernet and Low Power support all in a single chip. (vanepp) Feb 2021: converted to ESP32-C3-DevKitM-1. This chip is 30pins long (2 x15) and 11 pins width.
  YwRobot Breadboard Power Supply: The YwRobot Breadboard Power Supply (MB-V2) has two power rails; they can be 5V or 3V3. Power to the module can be provided through the female USB socket or through the A10 (female) 2.1mm power jack.
