# Fritzing sketch sketch-ir (saved by Fritzing 0.9.3b)

parts:
  M1 = ESP32-C3-DevKitM-1 [part_number=ESP32-C3-DevKitM-1]
  M2 = fc-51 [package=THT]

nets:
  N1: M1.GND-15, M1.GND-21, M2.pin2
  N2: M1.2, M2.pin1
  N3: M1.3, M2.pin3

custom parts:
  ESP32-C3-DevKitM-1: The DOIT Esp32 DevKit v1 is one of the development board created by DOIT to evaluate the ESP-WROOM-32 module. It is based on the ESP32 microcontroller that boasts Wifi, Bluetooth, Ethernet and Low Power support all in a single chip. (vanepp) Feb 2021: converted to ESP32-C3-DevKitM-1. This chip is 30pins long (2 x15) and 11 pins width.
