# Fritzing sketch sketch-vm (saved by Fritzing 0.9.3b)

parts:
  M1 = ESP32-C3-DevKitM-1 [part_number=ESP32-C3-DevKitM-1]
  hc-sr1 = hc-sr04
  YwRobot_Power_Supply1 = YwRobot Breadboard Power Supply [part_number=545043]
  VCC1 = Battery block 9V  # not connected
  R1 = Resistor [tolerance=±1% resistance=1 power=1W package=THT]
  VM1 = Multimeter (DC Voltage)

nets:
  N1: M1.GND-12, M1.GND-16, M1.GND-27, hc-sr1.GND, R1.Pin_0, VM1.V_Probe
  VCC: M1.3V3-17, M1.3V3-18, hc-sr1.VCC, YwRobot_Power_Supply1.VCC
  N2: M1.2, hc-sr1.Echo
  N3: M1.3, hc-sr1.Trig
  N4: YwRobot_Power_Supply1.GND, R1.Pin_1, VM1.COM_Probe

custom parts:
  ESP32-C3-DevKitM-1: The DOIT Esp32 DevKit v1 is one of the development board created by DOIT to evaluate the ESP-WROOM-32 module. It is based on the ESP32 microcontroller that boasts Wifi, Bluetooth, Ethernet and Low Power support all in a single chip. (vanepp) Feb 2021: converted to ESP32-C3-DevKitM-1. This chip is 30pins long (2 x15) and 11 pins width.
  YwRobot Breadboard Power Supply: The YwRobot Breadboard Power Supply (MB-V2) has two power rails; they can be 5V or 3V3. Power to the module can be provided through the female USB socket or through the A10 (female) 2.1mm power jack.
